# Fritzing sketch audio_proj (saved by Fritzing 1.0.5)
breadboards: 1

parts:
  Part3 = Arduino Nano (Rev3.0) (ICSP)
  DFRobot_DFPlayer_Mini1 = DFRobot DFPlayer Mini [part_number=DFR0299]
  R1 = Resistor [tolerance=±5% resistance=220 package="2010 [SMD]"]
  U1 = 3.5mm Audio Jack [package=audio-jack-3.5mm-smd]
  S2 = Round Pushbutton
  C1 = Tantalum Capacitor [capacitance="1 μF" voltage=35V package="A 3216 [SMD, tantalum]"]  # not connected
  C2 = Tantalum Capacitor [capacitance="1 μF" voltage=35V package="A 3216 [SMD, tantalum]"]  # not connected
  R2 = Resistor [tolerance=±5% resistance=220 package="2010 [SMD]"]

nets:
  GND: Part3.GND, DFRobot_DFPlayer_Mini1.GND-1, DFRobot_DFPlayer_Mini1.GND-2, S2.GND, R2.Pin_1
  N1: Part3.D4, S2.leg1
  N2: Part3.D10, DFRobot_DFPlayer_Mini1.TX
  N3: Part3.D11/MOSI, R1.Pin_1, R2.Pin_0
  5V: Part3.5V, DFRobot_DFPlayer_Mini1.VCC
  N4: DFRobot_DFPlayer_Mini1.RX, R1.Pin_0
  N5: DFRobot_DFPlayer_Mini1.DAC_R, U1.RIGHT
  N6: DFRobot_DFPlayer_Mini1.DAC_L, U1.LEFT

notes:
  Voltage Divider
  Resistor/Yellow - 1K
  Resistor/Grey - 2K
  Female Jack prongs
  1 - GND
  2 - Right
  3 - Left
  4 - Empty
  Capacitor
  (Stripe/Neg leg should face female jack, side)
  + => L/R
  - => jack Plug Prong

custom parts:
  Round Pushbutton: A generic pushbutton.
